# Fritzing sketch ESPNOW_Receiver (saved by Fritzing 0.9.10b)

parts:
  Bauteil1 = Adafruit QT Py ESP32-S2 [part_number="Adafruit #5325"]
  J1 = Basic Servo
  J2 = Basic Servo

nets:
  GND: Bauteil1.GND, J1.gnd, J2.gnd
  N1: Bauteil1.A0, J1.pulse
  N2: Bauteil1.A1, J2.pulse
  VCC: Bauteil1.+5V, J1.vcc, J2.vcc

custom parts:
  Adafruit QT Py ESP32-S2: What has your favorite Espressif WiFi microcontroller, comes with our favorite connector - the STEMMA QT, a chainable I2C port, and has lots of Flash and RAM memory for your next IoT project? What will make your next IoT project flyyyyy? What a cutie pie! Or is it... a QT Py? This diminutive dev board comes with one of our new favorite lil chips, the ESP32-S2! The ESP32-S2 is a highly-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
