# Fritzing sketch ESPNOW_Transmitter (saved by Fritzing 0.9.10b)

parts:
  A1 = XIAO ESP32C3-smd
  J1 = Basic Force Sensing Resistor (FSR) [package=THT]
  R1 = Resistor [tolerance=±5% power=0.25 resistance=10k package=THT]

nets:
  N1: A1.Pin_2, A1.Pin_21, R1.Pin_0
  N2: A1.Pin_9, J1.pin_0, R1.Pin_1
  N3: A1.Pin_20, J1.pin_1

notes:
  3.3V ->
  GND ->
  SCL ->
  SDA ->

custom parts:
  XIAO ESP32C3-smd: Seeed Studio XIAO ESP32C3 adopts new RISC-V architecture, supporting both Wi-Fi and BLE wireless connectivities.
